// Logisim project Project1.circ as structural Verilog: 16 circuits, main circuit Adder1bit
module Adder1bit (
  input  A,
  input  B,
  input  C_in,
  output S_out,
  output C_out
);

  wire and_1_out, and_2_out, xor_1_out;

  xor xor_1 (xor_1_out, A, B);
  and and_1 (and_1_out, A, B);
  xor xor_2 (S_out, xor_1_out, C_in);
  and and_2 (and_2_out, xor_1_out, C_in);
  or or_1 (C_out, and_2_out, and_1_out);
endmodule

module Adder4bits (
  input  [3:0] A,
  input  [3:0] B,
  input  C_in,
  output C_out,
  output Overflow,
  output [3:0] S
);

  wire adder1bit_1_c_out, adder1bit_2_c_out;

  Adder1bit adder1bit_1 (.A(A[0]), .B(B[0]), .C_in(C_in), .S_out(S[0]), .C_out(adder1bit_1_c_out));
  Adder1bit adder1bit_2 (.A(A[1]), .B(B[1]), .C_in(adder1bit_1_c_out), .S_out(A[2]), .C_out(adder1bit_2_c_out));
  Adder1bit adder1bit_3 (.A(A[2]), .B(B[2]), .C_in(adder1bit_2_c_out), .S_out(S[2]), .C_out(Overflow));
  Adder1bit adder1bit_4 (.A(A[3]), .B(B[3]), .C_in(Overflow), .S_out(S[3]), .C_out(C_out));

  assign S[1] = A[2];
endmodule

module Adder16bits (
  input  [15:0] A,
  input  [15:0] B,
  input  C_in,
  output C_out,
  output Overflow,
  output [15:0] S
);

  wire adder4bits_1_c_out, adder4bits_2_c_out, adder4bits_3_c_out;

  Adder4bits adder4bits_1 (
    .A(A[15:12]), .B(B[15:12]), .C_in(C_in), .C_out(adder4bits_1_c_out), .S(S[15:12]));  // open: Overflow
  Adder4bits adder4bits_2 (
    .A(A[11:8]), .B(B[11:8]), .C_in(adder4bits_1_c_out), .C_out(adder4bits_2_c_out), .S(S[11:8]));  // open: Overflow
  Adder4bits adder4bits_3 (
    .A(A[7:4]), .B(B[7:4]), .C_in(adder4bits_2_c_out), .C_out(adder4bits_3_c_out), .S(S[7:4]));  // open: Overflow
  Adder4bits adder4bits_4 (
    .A(A[3:0]), .B(B[3:0]), .C_in(adder4bits_3_c_out), .C_out(C_out), .Overflow(Overflow), .S(S[3:0]));
endmodule

module Add32 (
  input  [31:0] A,
  input  [31:0] B,
  input  Cin,
  output V,
  output [31:0] C
);

  wire adder16bits_1_c_out, adder16bits_2_c_out, adder16bits_2_overflow;

  Adder16bits adder16bits_1 (
    .A(A[31:16]), .B(B[31:16]), .C_in(Cin), .C_out(adder16bits_1_c_out), .S(C[31:16]));  // open: Overflow
  Adder16bits adder16bits_2 (
    .A(A[15:0]), .B(B[15:0]), .C_in(adder16bits_1_c_out), .C_out(adder16bits_2_c_out),
    .Overflow(adder16bits_2_overflow), .S(C[15:0]));
  xor xor_1 (V, adder16bits_2_c_out, adder16bits_2_overflow);
endmodule

module Shift1bit (
  input  Cin,
  input  [31:0] B,
  output [31:0] C
);


  assign C = {B[30:0], Cin};
endmodule

module Shift2bits (
  input  Cin,
  input  [31:0] B,
  output [31:0] C
);

  wire [31:0] shift1bit_1_c;

  Shift1bit shift1bit_1 (.Cin(Cin), .B(B), .C(shift1bit_1_c));
  Shift1bit shift1bit_2 (.Cin(Cin), .B(shift1bit_1_c), .C(C));
endmodule

module Shift4bits (
  input  Cin,
  input  [31:0] B,
  output [31:0] C
);

  wire [31:0] shift2bits_1_c;

  Shift2bits shift2bits_1 (.Cin(Cin), .B(B), .C(shift2bits_1_c));
  Shift2bits shift2bits_2 (.Cin(Cin), .B(shift2bits_1_c), .C(C));
endmodule

module Shift8bits (
  input  Cin,
  input  [31:0] B,
  output [31:0] C
);

  wire [31:0] shift4bits_1_c;

  Shift4bits shift4bits_1 (.Cin(Cin), .B(B), .C(shift4bits_1_c));
  Shift4bits shift4bits_2 (.Cin(Cin), .B(shift4bits_1_c), .C(C));
endmodule

module LeftShift32 (
  input  [31:0] B,
  input  Cin,
  input  [4:0] Sa,
  output [31:0] C
);

  wire [31:0] multiplexer_1_out, multiplexer_2_out, multiplexer_3_out, multiplexer_4_out, shift1bit_1_c,
       shift2bits_1_c, shift4bits_1_c, shift8bits_1_c, shift16bits_1_c;

  Shift1bit shift1bit_1 (.Cin(Cin), .B(B), .C(shift1bit_1_c));
  Multiplexer #(.width(32)) multiplexer_1 (.in0(B), .in1(shift1bit_1_c), .out(multiplexer_1_out), .sel(Sa[0]));
  Multiplexer #(.width(32)) multiplexer_2 (
    .in0(multiplexer_1_out), .in1(shift2bits_1_c), .out(multiplexer_2_out), .sel(Sa[1]));
  Shift2bits shift2bits_1 (.Cin(Cin), .C(shift2bits_1_c));  // open: B
  Shift4bits shift4bits_1 (.Cin(Cin), .B(multiplexer_2_out), .C(shift4bits_1_c));
  Multiplexer #(.width(32)) multiplexer_3 (
    .in0(multiplexer_2_out), .in1(shift4bits_1_c), .out(multiplexer_3_out), .sel(Sa[2]));
  Multiplexer #(.width(32)) multiplexer_4 (
    .in0(multiplexer_3_out), .in1(shift8bits_1_c), .out(multiplexer_4_out), .sel(Sa[3]));
  Shift8bits shift8bits_1 (.Cin(Cin), .B(multiplexer_3_out), .C(shift8bits_1_c));
  Multiplexer #(.width(32)) multiplexer_5 (.in0(multiplexer_4_out), .in1(shift16bits_1_c), .out(C), .sel(Sa[4]));
  Shift16bits shift16bits_1 (.Cin(Cin), .B(multiplexer_4_out), .C(shift16bits_1_c));
endmodule

module Shift16bits (
  input  Cin,
  input  [31:0] B,
  output [31:0] C
);

  wire [31:0] shift8bits_1_c;

  Shift8bits shift8bits_1 (.Cin(Cin), .B(B), .C(shift8bits_1_c));
  Shift8bits shift8bits_2 (.Cin(Cin), .B(shift8bits_1_c), .C(C));
endmodule

module Add (
  input  [31:0] A,
  input  [31:0] B,
  input  [3:0] Op,
  output V,
  output [31:0] C
);

  wire add32_1_v, and_1_out, and_2_out, or_1_out;
  wire [31:0] add32_1_c, bit_extender_1_out, bit_extender_2_out, xor_1_out;

  assign bit_extender_1_out = {{31{Op[2]}}, Op[2]};  // Bit_Extender bit_extender_1
  assign xor_1_out = B ^ bit_extender_1_out;  // XOR_Gate xor_1, 32 bits wide
  and and_1 (and_1_out, Op[1], Op[2], ~Op[3]);  // AND_Gate
  and and_2 (and_2_out, Op[1], ~Op[1], ~Op[1]);  // AND_Gate
  or or_1 (or_1_out, and_1_out, and_2_out);
  Add32 add32_1 (.A(A), .B(xor_1_out), .Cin(Op[2]), .V(add32_1_v), .C(add32_1_c));
  assign bit_extender_2_out = {{31{or_1_out}}, or_1_out};  // Bit_Extender bit_extender_2
  and and_3 (V, add32_1_v, or_1_out);
  assign C = add32_1_c & bit_extender_2_out;  // AND_Gate and_4, 32 bits wide
endmodule

module CompareOp (
  input  [31:0] A,
  input  [31:0] B,
  input  [3:0] Op,
  output [31:0] C
);

  wire and_1_out, and_2_out, and_4_out, not_5_out, or_1_out;
  wire [0:0] not_2_out;
  wire [31:0] and_3_out, and_5_out, bit_extender_1_out, bit_extender_2_out, bit_extender_3_out,
       bit_extender_4_out, not_1_out, not_3_out, not_4_out, not_6_out, xnor_1_out;

  assign not_1_out = ~A;  // NOT_Gate not_1, 32 bits wide
  assign xnor_1_out = ~B;  // XNOR_Gate xnor_1, 32 bits wide XNOR_Gate
  not not_2 (not_2_out[0], Op[0]);
  and and_1 (and_1_out, ~Op[1], ~Op[2], Op[3]);  // AND_Gate
  and and_2 (and_2_out, Op[1], ~Op[2], Op[3]);  // AND_Gate
  or or_1 (or_1_out, and_1_out, and_2_out);
  // AND_Gate and_3 has open pins: out=and_3_out
  // AND_Gate and_4 has open pins: out=and_4_out
  assign not_3_out = ~A;  // NOT_Gate not_3, 32 bits wide
  assign not_4_out = ~and_3_out;  // NOT_Gate not_4, 32 bits wide
  not not_5 (not_5_out, and_4_out);
  assign and_5_out = not_3_out & not_4_out;  // AND_Gate and_5, 32 bits wide
  Bit_Extender #(.in_width(32), .out_width(32)) bit_extender_1 (.in(not_6_out), .out(bit_extender_1_out));
  assign not_6_out = ~and_5_out;  // NOT_Gate not_6, 32 bits wide
  Bit_Extender #(.in_width(32), .out_width(32)) bit_extender_2 (.in(and_5_out), .out(bit_extender_2_out));
  assign bit_extender_3_out = {{31{not_5_out}}, not_5_out};  // Bit_Extender bit_extender_3
  assign bit_extender_4_out = {{31{and_4_out}}, and_4_out};  // Bit_Extender bit_extender_4
  Multiplexer #(.enable("true"), .select(2), .width(32)) multiplexer_1 (
    .in0(bit_extender_1_out), .in1(bit_extender_2_out), .in2(bit_extender_3_out), .in3(bit_extender_4_out),
    .out(C), .sel({Op[1], not_2_out[0]}), .en(or_1_out));
endmodule

module LogicOp (
  input  [31:0] A,
  input  [31:0] B,
  input  [3:0] Op,
  output [31:0] C
);

  wire and_2_out, and_3_out, or_2_out;
  wire [0:0] not_1_out;
  wire [31:0] and_1_out, nor_1_out, or_1_out, xor_1_out;

  assign or_1_out = A | B;  // OR_Gate or_1, 32 bits wide
  assign and_1_out = A & B;  // AND_Gate and_1, 32 bits wide
  assign nor_1_out = ~(A | B);  // NOR_Gate nor_1, 32 bits wide
  assign xor_1_out = A ^ B;  // XOR_Gate xor_1, 32 bits wide
  not not_1 (not_1_out[0], Op[0]);
  and and_2 (and_2_out, ~Op[1], ~Op[2], Op[3]);  // AND_Gate
  and and_3 (and_3_out, Op[1], ~Op[2], Op[3]);  // AND_Gate
  Multiplexer #(.enable("true"), .select(2), .width(32)) multiplexer_1 (
    .in0(or_1_out), .in1(and_1_out), .in2(nor_1_out), .in3(xor_1_out), .out(C), .sel({Op[1], not_1_out[0]}),
    .en(or_2_out));
  or or_2 (or_2_out, and_2_out, and_3_out);
endmodule

module Shift (
  input  [31:0] B,
  input  [3:0] Op,
  input  [4:0] Sa,
  output [31:0] C
);

  wire and_1_out, and_2_out, and_3_out, reverse_1_sign;
  wire [4:0] and_4_out, bit_extender_1_out;
  wire [31:0] leftshift32_1_c, multiplexer_1_out, reverse_1_b2, reverse_2_b2;

  and and_1 (and_1_out, Op[1], Op[3]);
  Reverse reverse_1 (.B1(B), .B2(reverse_1_b2), .Sign(reverse_1_sign));
  and and_2 (and_2_out, reverse_1_sign, Op[0]);
  and and_3 (and_3_out, and_2_out, Op[2]);
  Multiplexer #(.enable("true"), .width(32)) multiplexer_1 (
    .in0(B), .in1(reverse_1_b2), .out(multiplexer_1_out), .sel(Op[2]), .en(and_1_out));
  assign bit_extender_1_out = {{4{and_1_out}}, and_1_out};  // Bit_Extender bit_extender_1
  assign and_4_out = bit_extender_1_out & Sa;  // AND_Gate and_4, 5 bits wide
  LeftShift32 leftshift32_1 (.B(multiplexer_1_out), .Cin(and_3_out), .Sa(and_4_out), .C(leftshift32_1_c));
  Reverse reverse_2 (.B1(leftshift32_1_c), .B2(reverse_2_b2));  // open: Sign
  Multiplexer #(.width(32)) multiplexer_2 (.in0(leftshift32_1_c), .in1(reverse_2_b2), .out(C), .sel(Op[2]));
endmodule

module Reverse (
  input  [31:0] B1,
  output [31:0] B2,
  output Sign
);


  assign B2 = {B1[0], B1[1], B1[2], B1[3], B1[4], B1[5], B1[6], B1[7], B1[8], B1[9], B1[10], B1[11], B1[12], B1[13], B1[14], B1[15], B1[16], B1[17], B1[18], B1[19], B1[20], B1[21], B1[22], B1[23], B1[24], B1[25], B1[26], B1[27], B1[28], B1[29], B1[30], B1[31]};
  assign Sign = B1[31];
endmodule

module ALU32 (
  input  [31:0] A,
  input  [31:0] B,
  input  [3:0] Op,
  input  [4:0] Sa,
  output V,
  output [31:0] C
);

  wire [31:0] add_1_c, compareop_1_c, logicop_1_c, shift_1_c;

  CompareOp compareop_1 (.A(A), .B(B), .Op(Op), .C(compareop_1_c));
  Add add_1 (.A(A), .B(B), .Op(Op), .V(V), .C(add_1_c));
  LogicOp logicop_1 (.A(A), .B(B), .Op(Op), .C(logicop_1_c));
  Shift shift_1 (.B(B), .Op(Op), .Sa(Sa), .C(shift_1_c));
  assign C = logicop_1_c | add_1_c | shift_1_c | compareop_1_c;  // OR_Gate or_1, 32 bits wide
endmodule
